# Fritzing sketch AnalogOutputDemo-Schematics (saved by Fritzing 0.9.10b)
breadboards: 1

parts:
  R12 = Rotary Potentiometer (Small) [maximum_resistance=10kΩ knob_status=50% power=0.5W package=THT]
  LED1 = LED - 5mm [color="Red (633nm)" current=0.030 package="5 mm [THT]"]
  R13 = Resistor [tolerance=±1% resistance=220 package="1206 [SMD]"]
  R14 = Resistor [tolerance=±1% resistance=220 package="1206 [SMD]"]
  LED2 = LED - 5mm [color="Red (633nm)" current=0.030 package="5 mm [THT]"]
  R15 = Resistor [tolerance=±1% resistance=220 package="1206 [SMD]"]
  R1 = Rotary Potentiometer (Small) [maximum_resistance=10kΩ knob_status=50% power=0.5W package=THT]
  LED3 = LED - 5mm [color="Red (633nm)" current=0.030 package="5 mm [THT]"]

nets:
  GND: R12.leg1, R13.Pin_1, R15.Pin_1, R1.leg1
  A0 (input): R12.wiper, R1.wiper
  5V: R12.leg2, R1.leg2
  N1: LED1.cathode, R13.Pin_0
  D3 (PWM): LED1.anode, LED2.anode, LED3.anode
  N2: R14.Pin_0, LED2.cathode
  N3: R15.Pin_0, LED3.cathode

notes:
  Brightness Fade Setup
  Brightness Fade with Potentiometer
  Potentiometer Fade LED PWM Setup
  Analog Output
