# Fritzing sketch digital-logic-demo-schematics (saved by Fritzing 0.9.10b)
breadboards: 1

parts:
  HC-SR04_Sensor_1 = HC-SR04 Ultrasonic Distance Sensor

nets:
  5V: HC-SR04_Sensor_1.VCC
  D4: HC-SR04_Sensor_1.TRIG
  D3 ': HC-SR04_Sensor_1.ECHO
  GND: HC-SR04_Sensor_1.GND

notes:
  HC-SR04 Ultrasonic Distance Sensor
